// Logisim project lab12Regfile.circ as structural Verilog: 1 circuit, main circuit main
// CPU
module main (
  input  [1:0] RS,
  input  [1:0] RT,
  input  [1:0] RD,
  input  [7:0] RD_WRITE_VALUE,
  input  RD_WRITE_ENABLE,
  output [7:0] RS_READ_VALUE,
  output [7:0] RT_READ_VALUE,
  output [7:0] REG_0_VALUE,
  output [7:0] REG_1_VALUE,
  output [7:0] REG_2_VALUE,
  output [7:0] REG_3_VALUE
);

  wire clk;
  wire [7:0] in0, in1, in2, in3;

  Clock CLOCK (.out(clk));
  Demultiplexer #(.select(2), .width(8), .tristate("true")) demultiplexer_1 (
    .out0(in0), .out1(in1), .out2(in2), .out3(in3), .in(RD_WRITE_VALUE), .sel(RD), .en(RD_WRITE_ENABLE));
  Register reg0 (.D(in0), .Q(REG_0_VALUE));  // open: en, clk, clr
  Register reg1 (.D(in1), .Q(REG_1_VALUE), .clk(clk));  // open: en, clr
  Register reg2 (.D(in2), .Q(REG_2_VALUE), .clk(clk));  // open: en, clr
  Register reg3 (.D(in3), .Q(REG_3_VALUE), .clk(clk));  // open: en, clr
  Multiplexer #(.select(2), .width(8)) multiplexer_1 (
    .in0(REG_0_VALUE), .in1(REG_1_VALUE), .in2(REG_2_VALUE), .in3(REG_3_VALUE), .out(RS_READ_VALUE),
    .sel(RS), .en(RD_WRITE_ENABLE));
  Multiplexer #(.select(2), .width(8)) multiplexer_2 (
    .in0(REG_0_VALUE), .in1(REG_1_VALUE), .in2(REG_2_VALUE), .in3(REG_3_VALUE), .out(RT_READ_VALUE),
    .sel(RT), .en(RD_WRITE_ENABLE));

  // Other names for the same wires on the sheet: en = RD_WRITE_ENABLE; out0[7:0] = REG_0_VALUE;
  //   out1[7:0] = REG_1_VALUE; out2[7:0] = REG_2_VALUE; out3[7:0] = REG_3_VALUE
endmodule
